// Logisim project MIPS_MultiCycle.circ as structural Verilog
module main (
);

  wire controlunit_1_pcwrite;
  wire [31:0] PC_q;

  Register #(.width(32)) PC (.en(controlunit_1_pcwrite), .Q(PC_q));  // open: D, clk, clr
  Memory memory_1 ();
  Multiplexer #(.enable("false"), .width(32)) multiplexer_1 (.in0(PC_q));  // open: in1, out, sel
  Register #(.width(32)) InstructionRegister ();  // open: D, en, clk, Q, clr
  Register #(.width(32)) MemoryDataRegister ();  // open: D, en, clk, Q, clr
  ControlUnit controlunit_1 (.PCWrite(controlunit_1_pcwrite));  // open: PCWriteCond, IorD, MemRead, MemWrite, MemtoReg, IRWrite, CauseWrite, IntCause, EPCWrite, PCSource, ALUOp, ALUSrcA, ALUSrcB, RegWrite, RegDst, Op, Overflow
  SignExtend signextend_1 ();
  Multiplexer #(.enable("false"), .width(32)) multiplexer_2 ();  // open: in0, in1, out, sel
  Multiplexer #(.enable("false"), .width(32)) multiplexer_3 ();  // open: in0, in1, out, sel
  Registers RegFile ();
  ShiftL2 shiftl2_1 ();
  ShiftL2 shiftl2_2 ();
  Register #(.width(32)) A ();  // open: D, en, clk, Q, clr
  Register #(.width(32)) B ();  // open: D, en, clk, Q, clr
  Multiplexer #(.enable("false"), .width(32)) multiplexer_4 ();  // open: in0, in1, out, sel
  Multiplexer #(.enable("false"), .select(2), .width(32)) multiplexer_5 ();  // open: in0, in1, in2, in3, out, sel
  ALU alu_1 ();
  Multiplexer #(.enable("false"), .select(2), .width(32)) multiplexer_6 ();  // open: in0, in1, in2, in3, out, sel
  ALU_Control alu_control_1 ();
  Register #(.width(32)) ALUOut ();  // open: D, en, clk, Q, clr
  Multiplexer #(.enable("false"), .width(32)) multiplexer_7 ();  // open: in0, in1, out, sel
  Register #(.width(32)) EPC ();  // open: D, en, clk, Q, clr
  Register #(.width(32)) Cause ();  // open: D, en, clk, Q, clr
endmodule

module ControlUnit (
  input  [5:0] Op,
  input  Overflow,
  output PCWriteCond,
  output PCWrite,
  output IorD,
  output MemRead,
  output MemWrite,
  output MemtoReg,
  output IRWrite,
  output CauseWrite,
  output IntCause,
  output EPCWrite,
  output [1:0] PCSource,
  output [1:0] ALUOp,
  output ALUSrcA,
  output [1:0] ALUSrcB,
  output RegWrite,
  output RegDst
);

  wire and_2_out, and_3_out, and_4_out, and_6_out, and_7_out, and_13_out, and_14_out, and_15_out, and_16_out,
       and_18_out, and_19_out, and_20_out, and_21_out, and_22_out, and_23_out, and_24_out, and_25_out,
       and_26_out, and_27_out, and_29_out, and_30_out, and_31_out, and_32_out, and_33_out, and_34_out,
       and_35_out, and_36_out, and_37_out, and_38_out, and_39_out, and_40_out, and_41_out, and_42_out,
       and_43_out, and_44_out, and_45_out, and_46_out, and_47_out, and_48_out, and_49_out, and_50_out,
       and_51_out, and_52_out, and_53_out, clock_1_out, not_1_out, not_2_out, not_3_out, not_4_out,
       not_5_out, not_6_out, not_7_out, not_8_out, not_9_out, not_10_out;
  wire [3:0] or_13_out, StateReg_q;

  not not_1 (not_1_out, StateReg_q[3]);
  not not_2 (not_2_out, StateReg_q[2]);
  not not_3 (not_3_out, StateReg_q[1]);
  not not_4 (not_4_out, StateReg_q[0]);
  not not_5 (not_5_out, Op[5]);
  not not_6 (not_6_out, Op[4]);
  not not_7 (not_7_out, Op[3]);
  not not_8 (not_8_out, Op[2]);
  not not_9 (not_9_out, Op[1]);
  not not_10 (not_10_out, Op[0]);
  Clock clock_1 (.out(clock_1_out));
  Register #(.width(4)) StateReg (.D(or_13_out), .en(1'b1), .clk(clock_1_out), .Q(StateReg_q));  // open: clr
  and and_1 (PCWriteCond, StateReg_q[3], not_3_out, not_4_out);
  and and_2 (and_2_out, not_1_out, not_2_out, not_3_out, not_4_out);
  and and_3 (and_3_out, StateReg_q[3], StateReg_q[0]);
  and and_4 (and_4_out, StateReg_q[3], StateReg_q[1]);
  and and_5 (IorD, not_1_out, not_2_out, StateReg_q[1], StateReg_q[0]);
  and and_6 (and_6_out, not_1_out, not_2_out, not_3_out, not_4_out);
  and and_7 (and_7_out, not_1_out, not_2_out, StateReg_q[1], StateReg_q[0]);
  and and_8 (MemtoReg, StateReg_q[2], not_3_out, not_4_out);
  and and_9 (IRWrite, not_1_out, not_2_out, not_3_out, not_4_out);
  and and_10 (CauseWrite, StateReg_q[3], StateReg_q[1]);
  and and_11 (IntCause, StateReg_q[3], StateReg_q[1], StateReg_q[0]);
  and and_12 (EPCWrite, StateReg_q[3], StateReg_q[1]);
  and and_13 (and_13_out, StateReg_q[3], StateReg_q[0]);
  and and_14 (and_14_out, StateReg_q[3], StateReg_q[1]);
  and and_15 (and_15_out, StateReg_q[3], not_4_out);
  and and_16 (and_16_out, StateReg_q[3], StateReg_q[1]);
  and and_17 (ALUOp[1], StateReg_q[2], StateReg_q[1], not_4_out);
  and and_18 (and_18_out, StateReg_q[3], not_4_out);
  and and_19 (and_19_out, StateReg_q[3], StateReg_q[1]);
  and and_20 (and_20_out, not_1_out, StateReg_q[1], not_4_out);
  and and_21 (and_21_out, StateReg_q[3], not_3_out, not_4_out);
  and and_22 (and_22_out, not_1_out, not_2_out, not_3_out, StateReg_q[0]);
  and and_23 (and_23_out, not_1_out, not_2_out, StateReg_q[1], not_4_out);
  and and_24 (and_24_out, not_1_out, not_2_out, not_3_out);
  and and_25 (and_25_out, StateReg_q[3], StateReg_q[1]);
  and and_26 (and_26_out, StateReg_q[2], not_3_out, not_4_out);
  and and_27 (and_27_out, StateReg_q[2], StateReg_q[1], StateReg_q[0]);
  and and_28 (RegDst, StateReg_q[2], StateReg_q[1], StateReg_q[0]);
  and and_29 (and_29_out, not_1_out, not_2_out, not_3_out, StateReg_q[0], not_9_out, Op[0]);
  and and_30 (and_30_out, not_1_out, not_2_out, not_3_out, StateReg_q[0], not_5_out, Op[1]);
  and and_31 (and_31_out, not_1_out, not_2_out, not_3_out, StateReg_q[0], Op[1], not_10_out);
  and and_32 (and_32_out, not_1_out, not_2_out, not_3_out, StateReg_q[0], Op[2]);
  and and_33 (and_33_out, not_1_out, not_2_out, not_3_out, StateReg_q[0], Op[3], not_9_out);
  and and_34 (and_34_out, not_1_out, not_2_out, not_3_out, StateReg_q[0], Op[4]);
  and and_35 (and_35_out, not_1_out, not_2_out, not_3_out, StateReg_q[0], Op[5], not_9_out);
  and and_36 (and_36_out, StateReg_q[2], StateReg_q[1], StateReg_q[0], Overflow);
  and and_37 (and_37_out, not_1_out, not_2_out, StateReg_q[0], not_5_out, not_6_out, not_7_out, not_8_out, not_9_out, not_10_out);
  and and_38 (and_38_out, not_1_out, StateReg_q[1], not_4_out, Op[3]);
  and and_39 (and_39_out, not_1_out, not_2_out, StateReg_q[1], StateReg_q[0]);
  and and_40 (and_40_out, StateReg_q[2], StateReg_q[1], not_4_out);
  and and_41 (and_41_out, not_1_out, not_2_out, not_3_out, StateReg_q[0], not_8_out, not_9_out);
  and and_42 (and_42_out, not_1_out, not_2_out, not_3_out, StateReg_q[0], Op[0]);
  and and_43 (and_43_out, not_1_out, not_2_out, not_3_out, StateReg_q[0], Op[2], Op[1]);
  and and_44 (and_44_out, not_1_out, not_2_out, not_3_out, StateReg_q[0], Op[3]);
  and and_45 (and_45_out, not_1_out, not_2_out, not_3_out, StateReg_q[0], Op[4]);
  and and_46 (and_46_out, not_1_out, not_2_out, not_3_out, StateReg_q[0], Op[5]);
  and and_47 (and_47_out, not_1_out, StateReg_q[1], not_4_out, not_7_out);
  and and_48 (and_48_out, StateReg_q[2], StateReg_q[1], not_4_out);
  and and_49 (and_49_out, StateReg_q[2], StateReg_q[1], Overflow);
  and and_50 (and_50_out, not_1_out, not_2_out, not_4_out);
  and and_51 (and_51_out, not_1_out, not_2_out, not_3_out, not_5_out, not_6_out, not_7_out, not_8_out, Op[1], not_10_out);
  and and_52 (and_52_out, not_1_out, StateReg_q[1], not_4_out);
  and and_53 (and_53_out, StateReg_q[2], StateReg_q[1], Overflow);
  or or_1 (PCWrite, and_2_out, and_3_out, and_4_out);
  or or_2 (MemRead, and_6_out, and_7_out);
  or or_3 (PCSource[1], and_13_out, and_14_out);
  or or_4 (PCSource[0], and_15_out, and_16_out);
  or or_5 (ALUOp[0], and_18_out, and_19_out);
  or or_6 (ALUSrcA, and_20_out, and_21_out);
  or or_7 (ALUSrcB[1], and_22_out, and_23_out);
  or or_8 (ALUSrcB[0], and_24_out, and_25_out);
  or or_9 (RegWrite, and_26_out, and_27_out);
  or or_10 (or_13_out[3], and_29_out, and_30_out, and_31_out, and_32_out, and_33_out, and_34_out, and_35_out, and_36_out);
  or or_11 (or_13_out[2], and_37_out, and_38_out, and_39_out, and_40_out);
  or or_12 (or_13_out[1], and_41_out, and_42_out, and_43_out, and_44_out, and_45_out, and_46_out, and_47_out, and_48_out, and_49_out);
  or or_13 (or_13_out[0], and_50_out, and_51_out, and_52_out, and_53_out);

  assign MemWrite = 1'b0;

  // Notes on the sheet:
  //   Next State
endmodule
